# Fritzing sketch Diagrama-robot-bluetooth (saved by Fritzing 0.9.2b)

parts:
  Part1 = Arduino Uno (Rev3)
  BT1 = Bluetooth HC-06u [package=THT]
  BAT1 = BC9VPC [package=bc9vpc]  # not connected
  BAT2 = BC9VPC [package=bc9vpc]
  M1 = DC Motor  # not connected
  M2 = DC Motor
  S1 = H-Bridge with L298N

nets:
  N1: Part1.D10_PWM/SS, M2.pin_1, S1.IN4
  N2: Part1.D11_PWM/MOSI, S1.IN3
  N3: Part1.D12/MISO, S1.IN2
  N4: Part1.D13/SCK, S1.IN1
  N5: Part1.D0/RX, BT1.RXD
  N6: Part1.D1/TX, BT1.TXD
  N7: Part1.D5_PWM, S1.ENB
  N8: Part1.D6_PWM, S1.ENA
  5V: Part1.5V, BT1.VCC
  GND: Part1.GND, BT1.GND, BAT2.V-, S1.GND
  N9: BAT2.V+, S1.12V

custom parts:
  Bluetooth HC-06u: Bluetooth HC-06 - face up, pins down 16.5mm x 37.5mm PCB
  H-Bridge with L298N: h-bridge

// code stored in the sketch: Diagrama-robot-bluetooth.ino

