# Fritzing sketch Diagrama-robot-wifi (saved by Fritzing 0.9.2b)

parts:
  U1 = NodeMCU V3.0
  S1 = H-Bridge with L298N
  M1 = DC Motor
  M2 = DC Motor
  VCC1 = Battery block 9V

nets:
  N1: U1.D3, S1.IN3
  N2: U1.D4, S1.IN4
  N3: U1.D5, S1.ENA
  N4: U1.D6, S1.ENB
  N5: U1.D7, S1.IN1
  N6: U1.D8, S1.IN2
  GND: U1.GND, S1.GND, VCC1.-
  N7: S1.12V, VCC1.+
  N8: S1.M1-01, M1.pin_1
  N9: S1.M1-02, M1.pin_2
  N10: S1.M2-01, M2.pin_1
  N11: S1.M2-02, M2.pin_2

custom parts:
  NodeMCU V3.0: ESP8266 based NodeMCU
  H-Bridge with L298N: h-bridge
